// Digital circuit demux.dig as structural Verilog
module demux (
  input  S,
  input  Y,
  output A,
  output B
);

  Demultiplexer demultiplexer_1 (.sel(S), .in(Y), .out_0(A), .out_1(B));
endmodule
