// Digital circuit ex_decoder_nand.dig as structural Verilog
module ex_decoder_nand (
  input  A,
  input  B,
  output Y
);

  wire decoder_1_out_0, decoder_1_out_1, decoder_1_out_2;

  Decoder #(.Selector_Bits(2)) decoder_1 (
    .sel({B, A}), .out_0(decoder_1_out_0), .out_1(decoder_1_out_1), .out_2(decoder_1_out_2));  // open: out_3
  or or_1 (Y, decoder_1_out_0, decoder_1_out_1, decoder_1_out_2);
endmodule

/* Test case:
A B Y
0 0 1
0 1 1
1 0 1
1 1 0
*/
