// Digital circuit ex_decoder_or.dig as structural Verilog
module ex_decoder_or (
  input  A,
  input  B,
  output Y
);

  wire decoder_1_out_1, decoder_1_out_2, decoder_1_out_3;

  Decoder #(.Selector_Bits(2)) decoder_1 (
    .sel({B, A}), .out_1(decoder_1_out_1), .out_2(decoder_1_out_2), .out_3(decoder_1_out_3));  // open: out_0
  or or_1 (Y, decoder_1_out_1, decoder_1_out_2, decoder_1_out_3);
endmodule

/* Test case:
A B Y
0 0 0
0 1 1
1 0 1
1 1 1
*/
