// Digital circuit ex_mux_4_to_1.dig as structural Verilog
module ex_mux_4_to_1 (
  input  A,
  input  B,
  input  C,
  input  D,
  input  S_2,
  input  S_1,
  output Y
);

  wire multiplexer_1_out, multiplexer_2_out;

  Multiplexer multiplexer_1 (.sel(S_1), .in_0(A), .in_1(B), .out(multiplexer_1_out));
  Multiplexer multiplexer_2 (.sel(S_1), .in_0(C), .in_1(D), .out(multiplexer_2_out));
  Multiplexer multiplexer_3 (.sel(S_2), .in_0(multiplexer_1_out), .in_1(multiplexer_2_out), .out(Y));
endmodule

/* Test case:
S_2 S_1 A B C D Y
0 0 0 0 0 0 0
0 0 0 0 0 1 0
0 0 0 0 1 0 0
0 0 0 0 1 1 0
0 0 0 1 0 0 0
0 0 0 1 0 1 0
0 0 0 1 1 0 0
0 0 0 1 1 1 0
0 0 1 0 0 0 1
0 0 1 0 0 1 1 
0 0 1 0 1 0 1
0 0 1 0 1 1 1
0 0 1 1 0 0 1
0 0 1 1 0 1 1
0 0 1 1 1 0 1
0 0 1 1 1 1 1
0 1 0 0 0 0 0
0 1 0 0 0 1 0 
0 1 0 0 1 0 0
0 1 0 0 1 1 0
0 1 0 1 0 0 1
0 1 0 1 0 1 1
0 1 0 1 1 0 1
0 1 0 1 1 1 1
0 1 1 0 0 0 0
0 1 1 0 0 1 0
0 1 1 0 1 0 0
0 1 1 0 1 1 0
0 1 1 1 0 0 1
0 1 1 1 0 1 1
0 1 1 1 1 0 1
0 1 1 1 1 1 1
1 0 0 0 0 0 0
1 0 0 0 0 1 0
1 0 0 0 1 0 1
1 0 0 0 1 1 1
1 0 0 1 0 0 0
1 0 0 1 0 1 0
1 0 0 1 1 0 1
1 0 0 1 1 1 1
1 0 1 0 0 0 0
1 0 1 0 0 1 0
1 0 1 0 1 0 1
1 0 1 0 1 1 1
1 0 1 1 0 0 0
1 0 1 1 0 1 0
1 0 1 1 1 0 1
1 0 1 1 1 1 1
1 1 0 0 0 0 0
1 1 0 0 0 1 1
1 1 0 0 1 0 0
1 1 0 0 1 1 1
1 1 0 1 0 0 0
1 1 0 1 0 1 1
1 1 0 1 1 0 0
1 1 0 1 1 1 1
1 1 1 0 0 0 0
1 1 1 0 0 1 1
1 1 1 0 1 0 0
1 1 1 0 1 1 1
1 1 1 1 0 0 0
1 1 1 1 0 1 1
1 1 1 1 1 0 0
1 1 1 1 1 1 1
*/
