// Digital circuit ex_mux_xor.dig as structural Verilog
module ex_mux_xor (
  input  A,
  input  B,
  output Y
);

  Multiplexer #(.Selector_Bits(2)) multiplexer_1 (
    .sel({B, A}), .in_0(1'b0), .in_1(1'b1), .in_2(1'b1), .in_3(1'b0), .out(Y));
endmodule

/* Test case:
A B Y
0 0 0
0 1 1
1 0 1
1 1 0
*/
